// Logisim project control-logic.circ as structural Verilog: 1 circuit, main circuit control_logic
module control_logic (
  input  [31:0] inst,
  input  BrEq,
  input  BrLt,
  output PCSel,
  output RegWEn,
  output [2:0] ImmSel,
  output BrUn,
  output ASel,
  output BSel,
  output [3:0] ALUSel,
  output MemRW,
  output [1:0] WBSel,
  output CSRSel,
  output CSRWen
);

  wire and_1_out, and_2_out, and_3_out, and_4_out, and_5_out, and_6_out, and_7_out, not_1_out, not_2_out,
       not_3_out, not_4_out, not_5_out, not_6_out, or_1_out;

  not not_1 (not_1_out, inst[13]);
  and and_1 (and_1_out, inst[4], inst[14]);
  and and_2 (and_2_out, inst[12], not_1_out, inst[14], inst[30]);
  not not_2 (not_2_out, inst[3]);
  not not_3 (not_3_out, inst[6]);
  not not_4 (not_4_out, inst[2]);
  and and_3 (and_3_out, not_4_out, not_5_out);
  not not_5 (not_5_out, inst[5]);
  and and_4 (and_4_out, inst[4], inst[2]);
  not not_6 (not_6_out, inst[2]);
  and and_5 (and_5_out, not_6_out, inst[4], inst[5]);
  and and_6 (and_6_out, inst[30], inst[5]);
  and and_7 (and_7_out, inst[25], inst[5]);
  or or_1 (or_1_out, and_3_out, and_4_out, and_5_out);
  and and_8 (ALUSel[0], inst[12], inst[4]);
  and and_9 (ALUSel[1], inst[4], inst[13]);
  or or_2 (ALUSel[2], and_1_out, and_6_out);
  or or_3 (ALUSel[3], and_6_out, and_2_out, and_7_out);
  and and_10 (RegWEn, inst[0], inst[1], not_2_out, not_3_out, or_1_out);

  assign BrUn = inst[13];
  assign BSel = inst[5];

  // Other names for the same wires on the sheet: b0 = inst[0]; b1 = inst[1]; b2 = inst[2]; b3 = inst[3]; b4 = inst[4];
  //   b5 = inst[5]; b6 = inst[6]; b7 = inst[7]; b8 = inst[8]; b9 = inst[9]; b10 = inst[10]; b11 = inst[11];
  //   b12 = inst[12]; b13 = inst[13]; b14 = inst[14]; b15 = inst[15]; b16 = inst[16]; b17 = inst[17]; b18 = inst[18];
  //   b19 = inst[19]; b20 = inst[20]; b21 = inst[21]; b22 = inst[22]; b23 = inst[23]; b24 = inst[24]; b25 = inst[25];
  //   b26 = inst[26]; b27 = inst[27]; b28 = inst[28]; b29 = inst[29]; b30 = inst[30]; b31 = inst[31]

  // Notes on the sheet:
  //   INPUTS to your circuit
  //   DON'T CHANGE THE LOCATIONS OF THE INPUTS AND OUTPUTS!
  //   OUTPUT from your circuit
  //   Register Write Enable is set to 1 when the instruction is R-format or I-format or U-format
endmodule
