// Logisim project cpu.circ as structural Verilog: 1 circuit, main circuit cpu
module cpu (
  input  clk,
  input  [31:0] INSTRUCTION,
  input  [31:0] READ_DATA,
  output [31:0] WRITE_ADDRESS,
  output [31:0] PROGRAM_COUNTER,
  output [31:0] ra,
  output [31:0] sp,
  output [31:0] t0,
  output [31:0] t1,
  output [31:0] t2,
  output [31:0] s0,
  output [31:0] s1,
  output [31:0] a0,
  output [31:0] tohost,
  output [3:0] WRITE_ENABLE,
  output [31:0] WRITE_DATA
);

  wire alu_1_p1, alu_1_p5, alu_1_p8, alu_1_p9, alu_1_p11, ASel, BrEq, BrLt, BrUn, BSel, CSR_WE, CSRSel,
       MemRW, PCSel, regfile_1_p1, regfile_1_p9, regfile_1_p11, regfile_1_p23, regfile_1_p25, regfile_1_p27,
       RegWEn;
  wire [1:0] bit_extender_3_out, bit_extender_4_out, bit_extender_5_out, bit_extender_6_out,
       bit_extender_8_out, MemSel, WBSel;
  wire [2:0] control_logic_1_immsel;
  wire [3:0] ALUOp, bit_extender_11_out, multiplexer_6_out, shifter_1_out, shifter_2_out;
  wire [7:0] bit_extender_7_out, demultiplexer_1_out0, demultiplexer_1_out1, demultiplexer_1_out2,
       demultiplexer_1_out3, multiplexer_7_out;
  wire [11:0] bit_extender_2_out;
  wire [15:0] multiplexer_8_out;
  wire [31:0] adder_1_out, bit_extender_1_out, bit_extender_9_out, bit_extender_10_out, imm, LOAD_DATA,
       multiplexer_1_out, multiplexer_2_out, multiplexer_3_out, multiplexer_4_out, multiplexer_5_out,
       regfile_1_p21, ToWrite;

  control_logic control_logic_1 (
    .CSRWen(CSR_WE), .PCSel(PCSel), .RegWEn(RegWEn), .ImmSel(control_logic_1_immsel), .BrUn(BrUn),
    .ASel(ASel), .BSel(BSel), .ALUSel(ALUOp), .MemRW(MemRW), .WBSel(WBSel), .CSRSel(CSRSel),
    .inst(INSTRUCTION), .BrEq(BrEq), .BrLt(BrLt));
  Adder #(.width(32)) adder_1 (.a(PROGRAM_COUNTER), .b(32'h4), .out(adder_1_out));  // open: cin, cout
  Register #(.width(32)) PC (.D(multiplexer_1_out), .clk(clk), .Q(PROGRAM_COUNTER));  // open: en, clr
  Multiplexer #(.enable("false"), .width(32)) multiplexer_1 (
    .in0(adder_1_out), .in1(WRITE_ADDRESS), .out(multiplexer_1_out), .sel(PCSel));
  imm_gen imm_gen_1 (.inst(INSTRUCTION), .ImmSel(control_logic_1_immsel), .imm(imm));
  Multiplexer #(.enable("false"), .select(2), .width(32)) multiplexer_2 (
    .in0(WRITE_ADDRESS), .in1(LOAD_DATA), .in2(imm), .in3(adder_1_out), .out(multiplexer_2_out), .sel(WBSel));
  branch_comp branch_comp_1 (.rs1(regfile_1_p21), .rs2(ToWrite), .BrUn(BrUn), .BrEq(BrEq), .BrLt(BrLt));
  // regfile regfile_1: pin names not known; wires that end beside it: regfile_1_p1, INSTRUCTION[19:15], INSTRUCTION[24:20], INSTRUCTION[11:7], multiplexer_2_out, RegWEn, clk, regfile_1_p1, regfile_1_p9, regfile_1_p9, regfile_1_p11, regfile_1_p11, ra, sp, t0, t1, t2, s0, s1, a0, regfile_1_p21, ToWrite, regfile_1_p23, regfile_1_p23, regfile_1_p25, regfile_1_p25, regfile_1_p27
  assign bit_extender_1_out = {{27{INSTRUCTION[19]}}, INSTRUCTION[19:15]};  // Bit_Extender bit_extender_1
  Multiplexer #(.enable("false"), .width(32)) multiplexer_3 (
    .in0(regfile_1_p21), .in1(bit_extender_1_out), .out(multiplexer_3_out), .sel(CSRSel));
  Bit_Extender #(.in_width(32), .out_width(12)) bit_extender_2 (.in(imm), .out(bit_extender_2_out));
  Multiplexer #(.enable("false"), .width(32)) multiplexer_4 (
    .in0(regfile_1_p21), .in1(PROGRAM_COUNTER), .out(multiplexer_4_out), .sel(ASel));
  Multiplexer #(.enable("false"), .width(32)) multiplexer_5 (
    .in0(imm), .in1(ToWrite), .out(multiplexer_5_out), .sel(BSel));
  // csr csr_1: pin names not known; wires that end beside it: bit_extender_2_out, multiplexer_3_out, CSR_WE, clk, tohost
  // alu alu_1: pin names not known; wires that end beside it: alu_1_p1, alu_1_p1, multiplexer_4_out, multiplexer_5_out, alu_1_p5, ALUOp, WRITE_ADDRESS, alu_1_p8, alu_1_p9, alu_1_p9, alu_1_p11
  Shifter #(.width(4)) shifter_1 (.in(4'b0001), .\dist (bit_extender_3_out), .out(shifter_1_out));
  Bit_Extender #(.in_width(32), .out_width(2), .\type ("zero")) bit_extender_3 (
    .in(WRITE_ADDRESS), .out(bit_extender_3_out));
  Shifter #(.width(4)) shifter_2 (.in(4'b0011), .\dist (bit_extender_4_out), .out(shifter_2_out));
  Bit_Extender #(.in_width(32), .out_width(2), .\type ("zero")) bit_extender_4 (
    .in(WRITE_ADDRESS), .out(bit_extender_4_out));
  Bit_Extender #(.in_width(32), .out_width(2), .\type ("zero")) bit_extender_5 (
    .in(WRITE_ADDRESS), .out(bit_extender_5_out));
  Bit_Extender #(.in_width(32), .out_width(2), .\type ("zero")) bit_extender_6 (
    .in(WRITE_ADDRESS), .out(bit_extender_6_out));
  Bit_Extender #(.in_width(32), .out_width(8)) bit_extender_7 (.in(ToWrite), .out(bit_extender_7_out));
  Demultiplexer #(.enable("false"), .select(2), .width(8)) demultiplexer_1 (
    .out0(demultiplexer_1_out0), .out1(demultiplexer_1_out1), .out2(demultiplexer_1_out2),
    .out3(demultiplexer_1_out3), .in(bit_extender_7_out), .sel(bit_extender_8_out));
  Bit_Extender #(.in_width(32), .out_width(2), .\type ("zero")) bit_extender_8 (
    .in(WRITE_ADDRESS), .out(bit_extender_8_out));
  Multiplexer #(.enable("false"), .select(2), .width(4)) multiplexer_6 (
    .in0(shifter_1_out), .in1(shifter_2_out), .in2(4'b1111), .out(multiplexer_6_out), .sel(MemSel));  // open: in3
  assign bit_extender_9_out = {{24{multiplexer_7_out[7]}}, multiplexer_7_out};  // Bit_Extender bit_extender_9
  Multiplexer #(.enable("false"), .select(2), .width(8)) multiplexer_7 (
    .in0(READ_DATA[7:0]), .in1(READ_DATA[15:8]), .in2(READ_DATA[23:16]), .in3(READ_DATA[31:24]),
    .out(multiplexer_7_out), .sel(bit_extender_5_out));
  assign bit_extender_10_out = {{16{multiplexer_8_out[15]}}, multiplexer_8_out};  // Bit_Extender bit_extender_10
  Multiplexer #(.enable("false"), .select(2), .width(16)) multiplexer_8 (
    .in0(READ_DATA[15:0]), .in1(READ_DATA[23:8]), .in2(READ_DATA[31:16]), .out(multiplexer_8_out),
    .sel(bit_extender_6_out));  // open: in3
  assign bit_extender_11_out = {{3{MemRW}}, MemRW};  // Bit_Extender bit_extender_11
  assign WRITE_ENABLE = bit_extender_11_out & multiplexer_6_out;  // AND_Gate and_1, 4 bits wide
  Multiplexer #(.enable("false"), .select(2), .width(32)) multiplexer_9 (
    .in0(bit_extender_9_out), .in1(bit_extender_10_out), .in2(READ_DATA), .out(LOAD_DATA), .sel(MemSel));  // open: in3
  Multiplexer #(.enable("false"), .select(2), .width(32)) multiplexer_10 (
    .in0({demultiplexer_1_out3, demultiplexer_1_out2, demultiplexer_1_out1, demultiplexer_1_out0}),
    .in2(ToWrite), .out(WRITE_DATA), .sel(MemSel));  // open: in1, in3

  // Other names for the same wires on the sheet: ALURes[31:0] = WRITE_ADDRESS

  // Notes on the sheet:
  //   Output to IMEM
  //   IMEM (do **NOT** move this)
  //   Inputs from IMEM
  //   Inputs/Outputs for testing. Do **NOT** move these.
  //   Outputs To DMEM
  //   DMEM (do **NOT** move this)
  //   Inputs From DMEM
endmodule
